// Logisim project tabalho.circ as structural Verilog: 1 circuit, main circuit main
module main (
);

  wire and_1_out, and_2_out, and_3_out, and_4_out, and_5_out, and_6_out, clock_1_out, dipswitch_1_sw1,
       dipswitch_1_sw2, FF0_q, FF0_qn, FF1_q, FF1_qn, or_1_out;

  DipSwitch #(.number(2)) dipswitch_1 (.sw1(dipswitch_1_sw1), .sw2(dipswitch_1_sw2));
  and and_1 (and_1_out, FF1_q, dipswitch_1_sw1);
  and and_2 (and_2_out, dipswitch_1_sw2, FF1_qn);
  or or_1 (or_1_out, and_1_out, and_2_out);
  Clock clock_1 (.out(clock_1_out));
  J_K_Flip_Flop FF0 (.J(or_1_out), .K(1'b1), .clk(clock_1_out), .Q(FF0_q), .Qn(FF0_qn));  // open: preset, reset
  J_K_Flip_Flop FF1 (.J(FF0_q), .K(FF0_q), .clk(clock_1_out), .Q(FF1_q), .Qn(FF1_qn));  // open: preset, reset
  and and_3 (and_3_out, FF0_qn, FF1_qn);
  and and_4 (and_4_out, FF0_q, FF1_qn);
  and and_5 (and_5_out, FF1_q, FF0_qn);
  and and_6 (and_6_out, FF0_q, FF1_q);
  LED led_1 (.in(and_3_out));
  LED led_2 (.in(and_4_out));
  LED led_3 (.in(FF1_q));
  LED led_4 (.in(and_5_out));
  LED led_5 (.in(and_6_out));
  LED led_6 (.in(FF1_qn));
endmodule
